// Logisim project C3Animador.circ as structural Verilog: 2 circuits, main circuit C3
module C3 (
  output [2:0] Cont
);

  wire clock_1_out, d_ff_1_qn, d_ff_2_qn, d_ff_3_qn;

  // Probe on Cont
  Clock clock_1 (.out(clock_1_out));
  D_Flip_Flop d_ff_1 (.clk(clock_1_out), .D(d_ff_1_qn), .Q(Cont[0]), .Qn(d_ff_1_qn));  // open: preset, en, reset
  D_Flip_Flop d_ff_2 (.clk(d_ff_1_qn), .D(d_ff_2_qn), .Q(Cont[1]), .Qn(d_ff_2_qn));  // open: preset, en, reset
  D_Flip_Flop d_ff_3 (.clk(d_ff_2_qn), .D(d_ff_3_qn), .Q(Cont[2]), .Qn(d_ff_3_qn));  // open: preset, en, reset

  // Notes on the sheet:
  //   Clock
  //   DEC
endmodule

module Animador (
);

  wire clock_1_out;
  wire [2:0] c3_1_cont;
  wire [8:0] rom_1_data;

  C3 c3_1 (.Cont(c3_1_cont));
  Clock clock_1 (.out(clock_1_out));
  DotMatrix #(.matrixcols(3), .matrixrows(3)) dotmatrix_1 (
    .col0(rom_1_data[2:0]), .col1(rom_1_data[5:3]), .col2(rom_1_data[8:6]));
  ROM #(.addrWidth(3), .dataWidth(9)) rom_1 (.addr(c3_1_cont), .data(rom_1_data));  // open: sel

  // Notes on the sheet:
  //   contents of rom_1 (hex, n*v repeats v):
  //   100 20 4 2 1 8 40 80
endmodule
