// Logisim project C4Animador.circ as structural Verilog: 2 circuits, main circuit C4
module C4 (
  output [3:0] Cont
);

  wire and_1_out, clock_1_out, d_ff_1_qn, d_ff_2_qn, d_ff_3_qn, d_ff_4_qn;

  // Probe on Cont
  Clock clock_1 (.out(clock_1_out));
  D_Flip_Flop d_ff_1 (
    .clk(clock_1_out), .D(d_ff_1_qn), .Q(Cont[0]), .Qn(d_ff_1_qn), .reset(and_1_out));  // open: preset, en
  D_Flip_Flop d_ff_2 (
    .clk(d_ff_1_qn), .D(d_ff_2_qn), .Q(Cont[1]), .Qn(d_ff_2_qn), .reset(and_1_out));  // open: preset, en
  D_Flip_Flop d_ff_3 (
    .clk(d_ff_2_qn), .D(d_ff_3_qn), .Q(Cont[2]), .Qn(d_ff_3_qn), .reset(and_1_out));  // open: preset, en
  D_Flip_Flop d_ff_4 (
    .clk(d_ff_3_qn), .D(d_ff_4_qn), .Q(Cont[3]), .Qn(d_ff_4_qn), .reset(and_1_out));  // open: preset, en
  and and_1 (and_1_out, Cont[3], Cont[2], d_ff_2_qn, d_ff_1_qn);

  // Notes on the sheet:
  //   Clock
  //   DEC
endmodule

module Animador (
);

  wire clock_1_out;
  wire [3:0] C4_cont;
  wire [15:0] rom_1_data;

  Clock clock_1 (.out(clock_1_out));
  C4 C4 (.Cont(C4_cont));
  ROM #(.addrWidth(4), .dataWidth(16)) rom_1 (.addr(C4_cont), .data(rom_1_data));  // open: sel
  DotMatrix #(.matrixcols(4), .matrixrows(4)) dotmatrix_1 (
    .col0({rom_1_data[12], rom_1_data[13], rom_1_data[14], rom_1_data[15]}),
    .col1({rom_1_data[8], rom_1_data[9], rom_1_data[10], rom_1_data[11]}),
    .col2({rom_1_data[4], rom_1_data[5], rom_1_data[6], rom_1_data[7]}),
    .col3({rom_1_data[0], rom_1_data[1], rom_1_data[2], rom_1_data[3]}));

  // Notes on the sheet:
  //   contents of rom_1 (hex, n*v repeats v):
  //   fffe ffef feff efff dfff bfff 7fff f7ff ff7f fff7 fffb fffd
endmodule
