// Logisim project contadorassincrono.circ as structural Verilog: 1 circuit, main circuit main
module main (
);

  wire \and , and2, and3, and4, clock_1_out, clock_2_out, clock_3_out, clock_4_out, d_ff_1_qn, d_ff_2_qn,
       d_ff_3_qn, d_ff_4_qn, d_ff_5_qn, d_ff_6_qn, d_ff_7_qn, d_ff_8_qn, t_ff_3_qn, t_ff_6_qn, t_ff_7_qn,
       t_ff_8_qn, t_ff_9_qn, t_ff_10_qn;
  wire [3:0] d_ff_1_q, d_ff_5_q;
  wire [4:0] t_ff_1_q, t_ff_6_q;

  Clock clock_1 (.out(clock_1_out));
  D_Flip_Flop d_ff_1 (
    .clk(clock_1_out), .D(d_ff_1_qn), .Q(d_ff_1_q[0]), .Qn(d_ff_1_qn), .reset(\and ));  // open: preset, en
  // Probe on d_ff_1_q
  Clock clock_2 (.out(clock_2_out));
  // Probe on t_ff_1_q
  D_Flip_Flop d_ff_2 (
    .clk(d_ff_1_qn), .D(d_ff_2_qn), .Q(d_ff_1_q[1]), .Qn(d_ff_2_qn), .reset(\and ));  // open: preset, en
  T_Flip_Flop #(.trigger("falling")) t_ff_1 (
    .clk(clock_2_out), .T(1'b1), .Q(t_ff_1_q[0]), .preset(and3));  // open: Qn, reset, en
  and and_1 (\and , d_ff_1_q[0], d_ff_2_qn, d_ff_1_q[2], d_ff_1_q[3]);
  D_Flip_Flop d_ff_3 (
    .clk(d_ff_2_qn), .D(d_ff_3_qn), .Q(d_ff_1_q[2]), .Qn(d_ff_3_qn), .preset(\and ));  // open: en, reset
  T_Flip_Flop #(.trigger("falling")) t_ff_2 (
    .clk(t_ff_1_q[0]), .T(1'b1), .Q(t_ff_1_q[1]), .preset(and3));  // open: Qn, reset, en
  D_Flip_Flop d_ff_4 (
    .clk(d_ff_3_qn), .D(d_ff_4_qn), .Q(d_ff_1_q[3]), .Qn(d_ff_4_qn), .reset(\and ));  // open: preset, en
  and and_2 (and3, t_ff_1_q[0], t_ff_1_q[1], t_ff_3_qn, t_ff_1_q[3], t_ff_1_q[4]);
  T_Flip_Flop #(.trigger("falling")) t_ff_3 (
    .clk(t_ff_1_q[1]), .T(1'b1), .Q(t_ff_1_q[2]), .Qn(t_ff_3_qn), .preset(and3));  // open: reset, en
  T_Flip_Flop #(.trigger("falling")) t_ff_4 (
    .clk(t_ff_1_q[2]), .T(1'b1), .Q(t_ff_1_q[3]), .reset(and3));  // open: Qn, preset, en
  Clock clock_3 (.out(clock_3_out));
  T_Flip_Flop #(.trigger("falling")) t_ff_5 (
    .clk(t_ff_1_q[3]), .T(1'b1), .Q(t_ff_1_q[4]), .reset(and3));  // open: Qn, preset, en
  D_Flip_Flop #(.trigger("falling")) d_ff_5 (
    .clk(clock_3_out), .D(d_ff_5_qn), .Q(d_ff_5_q[0]), .Qn(d_ff_5_qn), .preset(and2));  // open: en, reset
  // Probe on d_ff_5_q
  D_Flip_Flop #(.trigger("falling")) d_ff_6 (
    .clk(d_ff_5_qn), .D(d_ff_6_qn), .Q(d_ff_5_q[1]), .Qn(d_ff_6_qn), .reset(and2));  // open: preset, en
  Clock clock_4 (.out(clock_4_out));
  // Probe on t_ff_6_q
  and and_3 (and2, d_ff_5_qn, d_ff_5_q[1], d_ff_7_qn, d_ff_8_qn);
  D_Flip_Flop #(.trigger("falling")) d_ff_7 (
    .clk(d_ff_6_qn), .D(d_ff_7_qn), .Q(d_ff_5_q[2]), .Qn(d_ff_7_qn), .preset(and2));  // open: en, reset
  T_Flip_Flop #(.trigger("falling")) t_ff_6 (
    .clk(clock_4_out), .T(1'b1), .Q(t_ff_6_q[0]), .Qn(t_ff_6_qn), .reset(and4));  // open: preset, en
  D_Flip_Flop #(.trigger("falling")) d_ff_8 (
    .clk(d_ff_7_qn), .D(d_ff_8_qn), .Q(d_ff_5_q[3]), .Qn(d_ff_8_qn), .preset(and2));  // open: en, reset
  T_Flip_Flop #(.trigger("falling")) t_ff_7 (
    .clk(t_ff_6_qn), .T(1'b1), .Q(t_ff_6_q[1]), .Qn(t_ff_7_qn), .reset(and4));  // open: preset, en
  and and_4 (and4, t_ff_6_qn, t_ff_7_qn, t_ff_6_q[2], t_ff_9_qn, t_ff_10_qn);
  T_Flip_Flop #(.trigger("falling")) t_ff_8 (
    .clk(t_ff_7_qn), .T(1'b1), .Q(t_ff_6_q[2]), .Qn(t_ff_8_qn), .preset(and4));  // open: reset, en
  T_Flip_Flop #(.trigger("falling")) t_ff_9 (
    .clk(t_ff_8_qn), .T(1'b1), .Q(t_ff_6_q[3]), .Qn(t_ff_9_qn), .preset(and4));  // open: reset, en
  T_Flip_Flop #(.trigger("falling")) t_ff_10 (
    .clk(t_ff_9_qn), .T(1'b1), .Q(t_ff_6_q[4]), .Qn(t_ff_10_qn), .preset(and4));  // open: reset, en

  // Notes on the sheet:
  //   contador assíncrono 4-12 D
  //   contador assincrono 7-26 T
  //   cond. partida 0100
  //   cond. parada 1100
  //   cond. partida 00111
  //   cond. parada 11010
  //   contador assíncrono 13-3 D
  //   sensível a borda de descida
  //   contador assincrono 7-26 T
  //   cond. partida 1101
  //   cond. parada 0011
  //   cond. partida 11100
  //   cond. parada 00101
endmodule
