// Logisim project contadoresSincronoJK.circ as structural Verilog: 2 circuits, main circuit contador assincrono JK crescente
module contador_assincrono_JK_crescente (
);

  wire clock_1_out, j_k_ff_1_qn, j_k_ff_2_qn, j_k_ff_3_qn;
  wire [2:0] j_k_ff_1_q;

  Clock clock_1 (.out(clock_1_out));
  // Probe on j_k_ff_1_q
  J_K_Flip_Flop j_k_ff_1 (
    .J(1'b1), .clk(clock_1_out), .K(1'b1), .Q(j_k_ff_1_q[0]), .Qn(j_k_ff_1_qn));  // open: preset, en, reset
  J_K_Flip_Flop j_k_ff_2 (
    .J(1'b1), .clk(j_k_ff_1_qn), .K(1'b1), .Q(j_k_ff_1_q[1]), .Qn(j_k_ff_2_qn));  // open: preset, en, reset
  J_K_Flip_Flop j_k_ff_3 (
    .J(1'b1), .clk(j_k_ff_2_qn), .K(1'b1), .Q(j_k_ff_1_q[2]), .Qn(j_k_ff_3_qn));  // open: preset, en, reset

  // Notes on the sheet:
  //   Contador assíncrono JK crescente
endmodule

module contador_assincrono_JK_decrescente (
);

  wire clock_1_out, j_k_ff_1_qn, j_k_ff_2_qn, j_k_ff_3_qn;
  wire [2:0] j_k_ff_1_q;

  Clock clock_1 (.out(clock_1_out));
  // Probe on j_k_ff_1_q
  J_K_Flip_Flop j_k_ff_1 (
    .J(1'b1), .clk(clock_1_out), .K(1'b1), .Q(j_k_ff_1_q[0]), .Qn(j_k_ff_1_qn));  // open: preset, en, reset
  J_K_Flip_Flop j_k_ff_2 (
    .J(1'b1), .clk(j_k_ff_1_q[0]), .K(1'b1), .Q(j_k_ff_1_q[1]), .Qn(j_k_ff_2_qn));  // open: preset, en, reset
  J_K_Flip_Flop j_k_ff_3 (
    .J(1'b1), .clk(j_k_ff_1_q[1]), .K(1'b1), .Q(j_k_ff_1_q[2]), .Qn(j_k_ff_3_qn));  // open: preset, en, reset

  // Notes on the sheet:
  //   Contador JK decrescente 
endmodule
