// Logisim project contadores_D_T_JK_assin&sinc.circ as structural Verilog: 4 circuits, main circuit contador assíncrono FF D
module \contador_assíncrono_FF_D  (
);

  wire clock_1_out, clock_2_out, d_ff_1_qn, d_ff_2_qn, d_ff_3_qn, d_ff_4_qn, d_ff_5_qn, d_ff_6_qn;
  wire [2:0] d_ff_1_q, d_ff_4_q;

  Clock clock_1 (.out(clock_1_out));
  // Probe on d_ff_1_q
  D_Flip_Flop d_ff_1 (.clk(clock_1_out), .D(d_ff_1_qn), .Q(d_ff_1_q[0]), .Qn(d_ff_1_qn));  // open: preset, en, reset
  D_Flip_Flop d_ff_2 (.clk(d_ff_1_qn), .D(d_ff_2_qn), .Q(d_ff_1_q[1]), .Qn(d_ff_2_qn));  // open: preset, en, reset
  D_Flip_Flop d_ff_3 (.clk(d_ff_2_qn), .D(d_ff_3_qn), .Q(d_ff_1_q[2]), .Qn(d_ff_3_qn));  // open: preset, en, reset
  Clock clock_2 (.out(clock_2_out));
  // Probe on d_ff_4_q
  D_Flip_Flop d_ff_4 (.clk(clock_2_out), .D(d_ff_4_qn), .Q(d_ff_4_q[0]), .Qn(d_ff_4_qn));  // open: preset, en, reset
  D_Flip_Flop d_ff_5 (.clk(d_ff_4_q[0]), .D(d_ff_5_qn), .Q(d_ff_4_q[1]), .Qn(d_ff_5_qn));  // open: preset, en, reset
  D_Flip_Flop d_ff_6 (.clk(d_ff_4_q[1]), .D(d_ff_6_qn), .Q(d_ff_4_q[2]), .Qn(d_ff_6_qn));  // open: preset, en, reset

  // Notes on the sheet:
  //   Contador assíncrono FF D crescente
  //   O clock do próximo FF é conectado ao Q/ do anterior
  //   Contador assíncrono FF D decrescente
  //   O clock do próximo FF é conectado ao Q do anterior
endmodule

module \contador_assíncrono_FF_T  (
);

  wire clock_1_out, clock_2_out, t_ff_3_qn;
  wire [1:0] t_ff_1_q, t_ff_3_q;

  Clock clock_1 (.out(clock_1_out));
  // Probe on t_ff_1_q
  T_Flip_Flop t_ff_1 (.clk(clock_1_out), .T(1'b1), .Q(t_ff_1_q[0]));  // open: Qn, preset, reset, en
  T_Flip_Flop t_ff_2 (.clk(clock_1_out), .T(t_ff_1_q[0]), .Q(t_ff_1_q[1]));  // open: Qn, preset, reset, en
  Clock clock_2 (.out(clock_2_out));
  // Probe on t_ff_3_q
  T_Flip_Flop t_ff_3 (.clk(clock_2_out), .T(1'b1), .Q(t_ff_3_q[0]), .Qn(t_ff_3_qn));  // open: preset, reset, en
  T_Flip_Flop t_ff_4 (.clk(clock_2_out), .T(t_ff_3_qn), .Q(t_ff_3_q[1]));  // open: Qn, preset, reset, en

  // Notes on the sheet:
  //   Contador assíncrono FF T crescente
  //   T do próximo conectado ao Q
  //   Contador assíncrono FF T decrescente
  //   T do próximo conectado ao Q/
endmodule

module contador_assincrono_FF_JK (
);

  wire clock_1_out, clock_2_out, j_k_ff_1_qn;
  wire [1:0] j_k_ff_1_q, j_k_ff_3_q;

  // Probe on j_k_ff_1_q
  Clock clock_1 (.out(clock_1_out));
  J_K_Flip_Flop j_k_ff_1 (
    .J(1'b1), .clk(clock_1_out), .K(1'b1), .Q(j_k_ff_1_q[0]), .Qn(j_k_ff_1_qn));  // open: preset, en, reset
  J_K_Flip_Flop j_k_ff_2 (.J(1'b1), .clk(j_k_ff_1_qn), .K(1'b1), .Q(j_k_ff_1_q[1]));  // open: Qn, preset, en, reset
  // Probe on j_k_ff_3_q
  Clock clock_2 (.out(clock_2_out));
  J_K_Flip_Flop j_k_ff_3 (.J(1'b1), .clk(clock_2_out), .K(1'b1), .Q(j_k_ff_3_q[0]));  // open: Qn, preset, en, reset
  J_K_Flip_Flop j_k_ff_4 (.J(1'b1), .clk(j_k_ff_3_q[0]), .K(1'b1), .Q(j_k_ff_3_q[1]));  // open: Qn, preset, en, reset

  // Notes on the sheet:
  //   Contador assíncrono FF JK crescente
  //   Clock do próximo do Q/ do anterior
  //   Contador assíncrono FF JK decrescente
  //   Clock do próximo do Q do anterior
endmodule

module \contador_síncrono_FF_D  (
);

  wire and_1_out, and_2_out, clock_1_out, d_ff_1_qn, S0, S1;
  wire [1:0] d_ff_1_q;

  // Probe on d_ff_1_q
  Clock clock_1 (.out(clock_1_out));
  D_Flip_Flop d_ff_1 (.clk(clock_1_out), .D(S0), .Q(d_ff_1_q[0]), .Qn(d_ff_1_qn));  // open: preset, en, reset
  D_Flip_Flop d_ff_2 (.clk(clock_1_out), .D(S1), .Q(d_ff_1_q[1]), .Qn(S1));  // open: preset, en, reset
  and and_1 (and_1_out, S1, d_ff_1_qn);
  or or_1 (S0, and_1_out, and_2_out);
  and and_2 (and_2_out, d_ff_1_q[1], d_ff_1_q[0]);

  // Notes on the sheet:
  //   atual
  //   0 0
  //   0 1
  //   1 0
  //   1 1
  //   ORDEM: 0, 3, 1, 2
  //   próx
  //   S1 S0
  //   1 1
  //   1 0
  //   0 0
  //   0 1
  //   S1 B/ B
  //   A/
  //   A
  //   S0 B/ B
  //   A/
  //   A
  //   1 1
  //   S1 = A/
  //    0 0
  //   S0 = A/B/ + AB
  //   1 0
  //   0 1
endmodule
