// Logisim project contadorsincrono.circ as structural Verilog: 1 circuit, main circuit main
module main (
);

  wire and_1_out, and_2_out, and_3_out, and_4_out, clock_1_out, D0, D1, D2, FF0_qn, FF1_qn, FF2_qn;
  wire [2:0] FF0_q;

  Clock clock_1 (.out(clock_1_out));
  // Probe on FF0_q
  D_Flip_Flop FF2 (.clk(clock_1_out), .D(D0), .Q(FF0_q[2]), .Qn(FF2_qn));  // open: preset, en, reset
  D_Flip_Flop FF1 (.clk(clock_1_out), .D(D1), .Q(FF0_q[1]), .Qn(FF1_qn));  // open: preset, en, reset
  D_Flip_Flop FF0 (.clk(clock_1_out), .D(D2), .Q(FF0_q[0]), .Qn(FF0_qn));  // open: preset, en, reset
  and and_1 (and_1_out, FF1_qn, FF0_q[0]);
  and and_2 (and_2_out, FF0_q[1], FF0_qn);
  and and_3 (and_3_out, FF0_q[2], FF1_qn);
  and and_4 (and_4_out, FF1_qn, FF0_q[0]);
  and and_5 (D0, FF1_qn, FF0_qn);
  or or_1 (D2, and_1_out, and_2_out);
  or or_2 (D1, and_3_out, and_4_out);
endmodule
