// Logisim project cs1.circ as structural Verilog: 1 circuit, main circuit main
module main (
);

  wire and_1_out, and_2_out, D0, D1, d_ff_1_q, d_ff_1_qn;
  wire [1:0] d_ff_2_q;

  Clock clock_1 (.out(d_ff_2_q[1]));
  // Probe on d_ff_2_q
  D_Flip_Flop d_ff_1 (.clk(d_ff_2_q[1]), .D(D0), .Q(d_ff_1_q), .Qn(d_ff_1_qn));  // open: preset, en, reset
  D_Flip_Flop d_ff_2 (.clk(d_ff_2_q[1]), .D(D1), .Q(d_ff_2_q[0]), .Qn(D1));  // open: preset, en, reset
  and and_1 (and_1_out, D1, d_ff_1_qn);
  and and_2 (and_2_out, d_ff_2_q[0], d_ff_1_q);
  or or_1 (D0, and_1_out, and_2_out);
endmodule
