// Logisim project cs2.circ as structural Verilog: 1 circuit, main circuit main
module main (
);

  wire and_1_out, and_2_out, and_3_out, and_4_out, and_5_out, and_6_out, clock_1_out, D0, D1, D2, d_ff_1_qn,
       d_ff_3_qn;
  wire [2:0] d_ff_1_q;

  Clock clock_1 (.out(clock_1_out));
  // Probe on d_ff_1_q
  D_Flip_Flop #(.trigger("falling")) d_ff_1 (
    .clk(clock_1_out), .D(D2), .Q(d_ff_1_q[0]), .Qn(d_ff_1_qn));  // open: preset, en, reset
  D_Flip_Flop #(.trigger("falling")) d_ff_2 (
    .clk(clock_1_out), .D(D1), .Q(d_ff_1_q[1]), .Qn(D1));  // open: preset, en, reset
  D_Flip_Flop #(.trigger("falling")) d_ff_3 (
    .clk(clock_1_out), .D(D0), .Q(d_ff_1_q[2]), .Qn(d_ff_3_qn));  // open: preset, en, reset
  and and_1 (and_1_out, D1, d_ff_1_q[0]);
  and and_2 (and_2_out, d_ff_1_q[1], d_ff_3_qn);
  and and_3 (and_3_out, d_ff_3_qn, D1, d_ff_1_qn);
  and and_4 (and_4_out, d_ff_3_qn, d_ff_1_q[1], d_ff_1_q[0]);
  and and_5 (and_5_out, d_ff_1_q[2], D1, d_ff_1_q[0]);
  and and_6 (and_6_out, d_ff_1_q[2], d_ff_1_q[1], d_ff_1_qn);
  or or_1 (D2, and_1_out, and_2_out);
  or or_2 (D0, and_3_out, and_4_out, and_5_out, and_6_out);
endmodule
