// Logisim project estudo.circ as structural Verilog: 3 circuits, main circuit 2 -> 14
module _2____14 (
);

  wire and_1_out, clock_1_out, d_ff_1_qn, d_ff_2_qn, d_ff_3_qn, d_ff_4_qn;
  wire [3:0] d_ff_1_q;

  Clock clock_1 (.out(clock_1_out));
  // Probe on d_ff_1_q
  D_Flip_Flop d_ff_1 (
    .clk(clock_1_out), .D(d_ff_1_qn), .Q(d_ff_1_q[0]), .Qn(d_ff_1_qn), .reset(and_1_out));  // open: preset, en
  D_Flip_Flop d_ff_2 (
    .clk(d_ff_1_qn), .D(d_ff_2_qn), .Q(d_ff_1_q[1]), .Qn(d_ff_2_qn), .preset(and_1_out));  // open: en, reset
  D_Flip_Flop d_ff_3 (
    .clk(d_ff_2_qn), .D(d_ff_3_qn), .Q(d_ff_1_q[2]), .Qn(d_ff_3_qn), .reset(and_1_out));  // open: preset, en
  D_Flip_Flop d_ff_4 (
    .clk(d_ff_3_qn), .D(d_ff_4_qn), .Q(d_ff_1_q[3]), .Qn(d_ff_4_qn), .reset(and_1_out));  // open: preset, en
  and and_1 (and_1_out, d_ff_1_q[0], d_ff_1_q[1], d_ff_1_q[2], d_ff_1_q[3]);

  // Notes on the sheet:
  //   2 -> 14
  //   0010
  //   1110
endmodule

module _7____22 (
);

  wire and_1_out, clock_1_out, d_ff_1_qn, d_ff_2_qn, d_ff_3_qn, d_ff_4_qn, d_ff_5_qn;
  wire [4:0] d_ff_1_q;

  Clock clock_1 (.out(clock_1_out));
  // Probe on d_ff_1_q
  D_Flip_Flop d_ff_1 (
    .clk(clock_1_out), .D(d_ff_1_qn), .Q(d_ff_1_q[0]), .Qn(d_ff_1_qn), .preset(and_1_out));  // open: en, reset
  D_Flip_Flop d_ff_2 (
    .clk(d_ff_1_qn), .D(d_ff_2_qn), .Q(d_ff_1_q[1]), .Qn(d_ff_2_qn), .preset(and_1_out));  // open: en, reset
  D_Flip_Flop d_ff_3 (
    .clk(d_ff_2_qn), .D(d_ff_3_qn), .Q(d_ff_1_q[2]), .Qn(d_ff_3_qn), .preset(and_1_out));  // open: en, reset
  D_Flip_Flop d_ff_4 (
    .clk(d_ff_3_qn), .D(d_ff_4_qn), .Q(d_ff_1_q[3]), .Qn(d_ff_4_qn), .reset(and_1_out));  // open: preset, en
  D_Flip_Flop d_ff_5 (
    .clk(d_ff_4_qn), .D(d_ff_5_qn), .Q(d_ff_1_q[4]), .Qn(d_ff_5_qn), .reset(and_1_out));  // open: preset, en
  and and_1 (and_1_out, d_ff_1_q[4], d_ff_4_qn, d_ff_1_q[2], d_ff_1_q[1], d_ff_1_q[0]);

  // Notes on the sheet:
  //   7 -> 22
  //   00111
  //   10110
endmodule

module _0_3_1_2_5_8_12 (
);

  wire and_1_out, and_2_out, and_3_out, and_4_out, and_5_out, and_6_out, and_7_out, and_8_out, and_9_out,
       and_10_out, and_11_out, and_12_out, and_13_out, and_14_out, and_15_out, clock_1_out, S0, S1, S2, S3,
       t_ff_1_qn, t_ff_2_qn, t_ff_3_qn, t_ff_4_qn;
  wire [3:0] t_ff_1_q;

  Clock clock_1 (.out(clock_1_out));
  // Probe on t_ff_1_q
  T_Flip_Flop t_ff_1 (.clk(clock_1_out), .T(S3), .Q(t_ff_1_q[0]), .Qn(t_ff_1_qn));  // open: preset, reset, en
  T_Flip_Flop t_ff_2 (.clk(clock_1_out), .T(S2), .Q(t_ff_1_q[1]), .Qn(t_ff_2_qn));  // open: preset, reset, en
  T_Flip_Flop t_ff_3 (.clk(clock_1_out), .T(S1), .Q(t_ff_1_q[2]), .Qn(t_ff_3_qn));  // open: preset, reset, en
  T_Flip_Flop t_ff_4 (.clk(clock_1_out), .T(S0), .Q(t_ff_1_q[3]), .Qn(t_ff_4_qn));  // open: preset, reset, en
  and and_1 (and_1_out, t_ff_1_q[3], t_ff_1_q[2], t_ff_2_qn, t_ff_1_qn);
  and and_2 (and_2_out, t_ff_4_qn, t_ff_1_q[2], t_ff_1_q[0]);
  and and_3 (and_3_out, t_ff_1_q[2], t_ff_1_q[1], t_ff_1_q[0]);
  and and_4 (and_4_out, t_ff_1_q[3], t_ff_2_qn, t_ff_1_qn);
  and and_5 (and_5_out, t_ff_4_qn, t_ff_1_q[2], t_ff_1_q[0]);
  and and_6 (and_6_out, t_ff_1_q[3], t_ff_1_q[1], t_ff_1_q[0]);
  and and_7 (and_7_out, t_ff_4_qn, t_ff_3_qn, t_ff_1_q[1], t_ff_1_qn);
  and and_8 (and_8_out, t_ff_4_qn, t_ff_3_qn);
  and and_9 (and_9_out, t_ff_4_qn, t_ff_2_qn, t_ff_1_qn);
  and and_10 (and_10_out, t_ff_1_q[3], t_ff_1_q[0]);
  and and_11 (and_11_out, t_ff_1_q[1], t_ff_1_q[0]);
  and and_12 (and_12_out, t_ff_4_qn, t_ff_2_qn);
  and and_13 (and_13_out, t_ff_1_q[1], t_ff_1_q[0]);
  and and_14 (and_14_out, t_ff_1_q[3], t_ff_1_q[1]);
  and and_15 (and_15_out, t_ff_1_q[1], t_ff_1_qn);
  or or_1 (S0, and_1_out, and_2_out, and_3_out);
  or or_2 (S1, and_4_out, and_5_out, and_6_out, and_7_out);
  or or_3 (S2, and_8_out, and_9_out, and_10_out, and_11_out);
  or or_4 (S3, and_12_out, and_13_out, and_14_out, and_15_out);
endmodule
