// Logisim project lista17_cs1.circ as structural Verilog: 3 circuits, main circuit a
module a (
);

  wire clock_1_out, S0, t_ff_1_qn;
  wire [1:0] t_ff_1_q;

  // Probe on t_ff_1_q
  Clock clock_1 (.out(clock_1_out));
  T_Flip_Flop t_ff_1 (.clk(clock_1_out), .T(S0), .Q(t_ff_1_q[0]), .Qn(t_ff_1_qn));  // open: preset, reset, en
  T_Flip_Flop t_ff_2 (.clk(clock_1_out), .T(1'b1), .Q(t_ff_1_q[1]), .Qn(S0));  // open: preset, reset, en

  // Notes on the sheet:
  //   S1
endmodule

module b (
);

  wire and_1_out, and_2_out, and_3_out, and_4_out, clock_1_out, S0, S2, t_ff_1_qn, t_ff_2_qn, t_ff_3_qn;
  wire [2:0] t_ff_1_q;

  Clock clock_1 (.out(clock_1_out));
  // Probe on t_ff_1_q
  T_Flip_Flop t_ff_1 (.clk(clock_1_out), .T(S0), .Q(t_ff_1_q[0]), .Qn(t_ff_1_qn));  // open: preset, reset, en
  T_Flip_Flop t_ff_2 (.clk(clock_1_out), .T(1'b1), .Q(t_ff_1_q[1]), .Qn(t_ff_2_qn));  // open: preset, reset, en
  T_Flip_Flop t_ff_3 (.clk(clock_1_out), .T(S2), .Q(t_ff_1_q[2]), .Qn(t_ff_3_qn));  // open: preset, reset, en
  and and_1 (and_1_out, t_ff_2_qn, t_ff_1_qn);
  or or_1 (S2, and_1_out, and_2_out);
  and and_2 (and_2_out, t_ff_1_q[1], t_ff_1_q[0]);
  and and_3 (and_3_out, t_ff_3_qn, t_ff_1_q[1], t_ff_1_qn);
  or or_2 (S0, and_3_out, and_4_out);
  and and_4 (and_4_out, t_ff_1_q[2], t_ff_1_q[1], t_ff_1_q[0]);

  // Notes on the sheet:
  //   S1
endmodule

module c (
);

  wire and_1_out, and_2_out, and_3_out, and_4_out, clock_1_out, S0, S1, S2, t_ff_1_qn, t_ff_2_qn, t_ff_3_qn;
  wire [2:0] t_ff_1_q;

  Clock clock_1 (.out(clock_1_out));
  // Probe on t_ff_1_q
  T_Flip_Flop t_ff_1 (.clk(clock_1_out), .T(S0), .Q(t_ff_1_q[0]), .Qn(t_ff_1_qn));  // open: preset, reset, en
  T_Flip_Flop t_ff_2 (.clk(clock_1_out), .T(S1), .Q(t_ff_1_q[1]), .Qn(t_ff_2_qn));  // open: preset, reset, en
  T_Flip_Flop t_ff_3 (.clk(clock_1_out), .T(S2), .Q(t_ff_1_q[2]), .Qn(t_ff_3_qn));  // open: preset, reset, en
  and and_1 (and_1_out, t_ff_3_qn, t_ff_2_qn, t_ff_1_qn);
  or or_1 (S2, and_1_out, and_2_out);
  and and_2 (and_2_out, t_ff_1_q[2], t_ff_1_q[1]);
  or or_2 (S1, t_ff_1_q[1], t_ff_1_q[0], and_3_out);
  and and_3 (and_3_out, t_ff_1_q[2], t_ff_2_qn);
  or or_3 (S0, t_ff_1_q[1], and_4_out);
  and and_4 (and_4_out, t_ff_1_q[2], t_ff_1_q[0]);
endmodule
