// Logisim project sd.circ as structural Verilog: 1 circuit, main circuit main
module main (
  input  in_1,
  input  in_2,
  input  in_3,
  input  in_4,
  input  in_5,
  input  in_6
);

  wire clock_1_out, clock_2_out, clock_3_out, clock_4_out, clock_5_out, clock_6_out, d_ff_1_q, d_ff_2_q,
       d_ff_3_q, d_ff_5_q, j_k_ff_6_q, j_k_ff_6_qn, j_k_ff_7_q, j_k_ff_7_qn, j_k_ff_8_q, j_k_ff_8_qn,
       j_k_ff_9_q, j_k_ff_11_q, j_k_ff_12_q, j_k_ff_13_q, not_1_out, not_2_out, not_3_out, not_4_out,
       not_5_out, not_6_out, not_7_out, not_8_out, not_9_out, not_10_out, not_11_out, not_12_out, not_13_out,
       not_14_out, not_15_out, not_16_out, not_17_out, not_18_out, not_19_out, t_ff_5_q, t_ff_6_q, t_ff_7_q;
  wire [3:0] t_ff_1_q, t_ff_5_qn;
  wire [4:0] j_k_ff_1_q, j_k_ff_9_qn;

  Clock clock_1 (.out(clock_1_out));
  Clock clock_2 (.out(clock_2_out));
  Clock clock_3 (.out(clock_3_out));
  D_Flip_Flop d_ff_1 (.clk(clock_1_out), .D(in_2), .Q(d_ff_1_q));  // open: Qn, preset, en, reset
  not not_1 (not_1_out, clock_2_out);
  T_Flip_Flop t_ff_1 (.clk(not_1_out), .T(in_3), .Q(t_ff_1_q[0]));  // open: Qn, preset, reset, en
  // Probe on t_ff_1_q
  not not_2 (not_2_out, clock_3_out);
  D_Flip_Flop d_ff_2 (.clk(clock_1_out), .D(d_ff_1_q), .Q(d_ff_2_q));  // open: Qn, preset, en, reset
  not not_3 (not_3_out, t_ff_1_q[0]);
  T_Flip_Flop t_ff_2 (.clk(not_3_out), .T(in_3), .Q(t_ff_1_q[1]));  // open: Qn, preset, reset, en
  // Probe on j_k_ff_1_q
  J_K_Flip_Flop j_k_ff_1 (.J(in_6), .clk(not_2_out), .K(in_6), .Q(j_k_ff_1_q[0]));  // open: Qn, preset, en, reset
  not not_4 (not_4_out, j_k_ff_1_q[0]);
  D_Flip_Flop d_ff_3 (.clk(clock_1_out), .D(d_ff_2_q), .Q(d_ff_3_q));  // open: Qn, preset, en, reset
  not not_5 (not_5_out, t_ff_1_q[1]);
  J_K_Flip_Flop j_k_ff_2 (.J(in_6), .clk(not_4_out), .K(in_6), .Q(j_k_ff_1_q[1]));  // open: Qn, preset, en, reset
  not not_6 (not_6_out, j_k_ff_1_q[1]);
  D_Flip_Flop d_ff_4 (.clk(clock_1_out), .D(d_ff_5_q));  // open: Q, Qn, preset, en, reset
  D_Flip_Flop d_ff_5 (.clk(clock_1_out), .D(d_ff_3_q), .Q(d_ff_5_q));  // open: Qn, preset, en, reset
  not not_7 (not_7_out, t_ff_1_q[2]);
  T_Flip_Flop t_ff_3 (.clk(not_5_out), .T(in_3), .Q(t_ff_1_q[2]));  // open: Qn, preset, reset, en
  J_K_Flip_Flop j_k_ff_3 (.J(in_6), .clk(not_6_out), .K(in_6), .Q(j_k_ff_1_q[2]));  // open: Qn, preset, en, reset
  T_Flip_Flop t_ff_4 (.clk(not_7_out), .T(in_3), .Q(t_ff_1_q[3]));  // open: Qn, preset, reset, en
  J_K_Flip_Flop j_k_ff_4 (.J(in_6), .clk(not_8_out), .K(in_6), .Q(j_k_ff_1_q[3]));  // open: Qn, preset, en, reset
  not not_8 (not_8_out, j_k_ff_1_q[2]);
  Clock clock_4 (.out(clock_4_out));
  not not_9 (not_9_out, in_1);
  Clock clock_5 (.out(clock_5_out));
  J_K_Flip_Flop j_k_ff_5 (.J(in_6), .clk(not_10_out), .K(in_6), .Q(j_k_ff_1_q[4]));  // open: Qn, preset, en, reset
  not not_10 (not_10_out, j_k_ff_1_q[3]);
  J_K_Flip_Flop j_k_ff_6 (
    .J(in_1), .clk(clock_4_out), .K(not_9_out), .Q(j_k_ff_6_q), .Qn(j_k_ff_6_qn));  // open: preset, en, reset
  not not_11 (not_11_out, clock_5_out);
  Clock clock_6 (.out(clock_6_out));
  J_K_Flip_Flop j_k_ff_7 (
    .J(j_k_ff_6_q), .clk(clock_4_out), .K(j_k_ff_6_qn), .Q(j_k_ff_7_q), .Qn(j_k_ff_7_qn));  // open: preset, en, reset
  T_Flip_Flop t_ff_5 (.clk(not_11_out), .T(in_4), .Q(t_ff_5_q), .Qn(t_ff_5_qn[0]));  // open: preset, reset, en
  not not_12 (not_12_out, t_ff_5_q);
  J_K_Flip_Flop j_k_ff_8 (
    .J(j_k_ff_7_q), .clk(clock_4_out), .K(j_k_ff_7_qn), .Q(j_k_ff_8_q), .Qn(j_k_ff_8_qn));  // open: preset, en, reset
  T_Flip_Flop t_ff_6 (.clk(not_12_out), .T(in_4), .Q(t_ff_6_q), .Qn(t_ff_5_qn[1]));  // open: preset, reset, en
  not not_13 (not_13_out, t_ff_6_q);
  // Probe on t_ff_5_qn
  J_K_Flip_Flop j_k_ff_9 (
    .J(in_5), .clk(not_14_out), .K(in_5), .Q(j_k_ff_9_q), .Qn(j_k_ff_9_qn[0]));  // open: preset, en, reset
  not not_14 (not_14_out, clock_6_out);
  J_K_Flip_Flop j_k_ff_10 (.J(j_k_ff_8_q), .clk(clock_4_out), .K(j_k_ff_8_qn));  // open: Q, Qn, preset, en, reset
  T_Flip_Flop t_ff_7 (.clk(not_13_out), .T(in_4), .Q(t_ff_7_q), .Qn(t_ff_5_qn[2]));  // open: preset, reset, en
  not not_15 (not_15_out, t_ff_7_q);
  J_K_Flip_Flop j_k_ff_11 (
    .J(in_5), .clk(not_16_out), .K(in_5), .Q(j_k_ff_11_q), .Qn(j_k_ff_9_qn[1]));  // open: preset, en, reset
  not not_16 (not_16_out, j_k_ff_9_q);
  // Probe on j_k_ff_9_qn
  T_Flip_Flop t_ff_8 (.clk(not_15_out), .T(in_4), .Qn(t_ff_5_qn[3]));  // open: Q, preset, reset, en
  J_K_Flip_Flop j_k_ff_12 (
    .J(in_5), .clk(not_17_out), .K(in_5), .Q(j_k_ff_12_q), .Qn(j_k_ff_9_qn[2]));  // open: preset, en, reset
  not not_17 (not_17_out, j_k_ff_11_q);
  J_K_Flip_Flop j_k_ff_13 (
    .J(in_5), .clk(not_18_out), .K(in_5), .Q(j_k_ff_13_q), .Qn(j_k_ff_9_qn[3]));  // open: preset, en, reset
  not not_18 (not_18_out, j_k_ff_12_q);
  not not_19 (not_19_out, j_k_ff_13_q);
  J_K_Flip_Flop j_k_ff_14 (.J(in_5), .clk(not_19_out), .K(in_5), .Qn(j_k_ff_9_qn[4]));  // open: Q, preset, en, reset

  // Notes on the sheet:
  //   Registrador D
  //   Contador crescente 0-15 T
  //   Contador crescente 0-31 JK
  //   Registrador JK
  //   Contador decrescente 15-0 T
  //   Contador decrescente 31-0 JK
endmodule
